# Fritzing sketch ESP8266 Facebook Counter (saved by Fritzing 0.9.3b)

parts:
  WeMos_D1_Mini1 = WeMos D1 Mini
  J2 = male pin header, 5 pins [form="♂ (male)"]
  U1 = 7-SEGMENT-4DIGIT [package=7-segment-4digit]  # not connected
  U2 = 7-SEGMENT-4DIGIT [package=7-segment-4digit]  # not connected

nets:
  N1: WeMos_D1_Mini1.5V, J2.pin5
  N2: WeMos_D1_Mini1.D5, J2.pin3
  N3: WeMos_D1_Mini1.D6, J2.pin2
  N4: WeMos_D1_Mini1.D7, J2.pin4
  N5: WeMos_D1_Mini1.G, J2.pin1

notes:
  VCC
  DIN
  LOAD
  CLK
  GND

custom parts:
  WeMos D1 Mini: The D1 mini is a mini wifi board based on ESP-8266EX.
